# Fritzing sketch connexions Arduino 1 (saved by Fritzing 0.9.3b)
breadboards: 1

parts:
  Raspberry_Pi_1 = Raspberry Pi 3 [part_number=RPI-3-V1.2]
  Composant1 = Motor Driver 1A Dual TB6612FNG  # not connected
  Composant2 = Arduino Nano (Rev3.0) (ICSP)
  M2 = DC Motor  # not connected
  M3 = DC Motor  # not connected

nets:
  GND: Raspberry_Pi_1.GND, Composant2.GND
